// Logisim project lab1-2.2.circ as structural Verilog: 1 circuit, main circuit main
module main (
  input  D,
  input  D_2,
  input  [2:0] in_3,
  input  in_4,
  input  in_5,
  output Q,
  output D_3,
  output Q_2,
  output [2:0] out_9
);

  wire and_1_out, and_2_out, clock_2_out, clock_3_out, Clock_out, not_1_out;

  Clock Clock (.out(Clock_out));
  Clock clock_2 (.out(clock_2_out));
  not not_1 (not_1_out, D);
  D_Flip_Flop D_flipflop (.clk(clock_2_out), .D(D_2), .Q(Q_2));  // open: Qn, preset, en, reset
  and and_1 (and_1_out, not_1_out, Clock_out);
  and and_2 (and_2_out, Clock_out, D);
  nor nor_1 (Q, and_1_out, D_3);
  nor nor_2 (D_3, Q, and_2_out);
  Clock clock_3 (.out(clock_3_out));
  Register #(.width(3)) register_1 (.D(in_3), .en(in_4), .Q(out_9), .clk(clock_3_out), .clr(in_5));

  // Notes on the sheet:
  //   D latch
endmodule
