// Logisim project lab1-3.2.circ as structural Verilog: 1 circuit, main circuit main
module main (
  input  in_1,
  input  in_2,
  input  in_3,
  input  in_4,
  output out_5,
  output out_6,
  output out_7,
  output out_8
);

  wire clock_1_out;

  Clock clock_1 (.out(clock_1_out));
  Register #(.width(4)) register_1 (
    .D({in_4, in_3, in_2, in_1}), .en(1'b1), .Q({out_8, out_7, out_6, out_5}), .clk(clock_1_out));  // open: clr
endmodule
