// Logisim project lab2-3.1.circ as structural Verilog: 1 circuit, main circuit main
module main (
  input  [7:0] in_1,
  input  [7:0] in_2,
  input  [2:0] in_3,
  output [7:0] out_4
);

  wire [7:0] adder_1_out, adder_2_out, and_1_out, not_1_out, or_1_out, subtractor_1_out, subtractor_2_out,
       xor_1_out;

  assign not_1_out = ~in_1;  // NOT_Gate not_1, 8 bits wide
  Adder adder_1 (.a(in_1), .b(in_2), .out(adder_1_out));  // open: cin, cout
  Adder adder_2 (.a(in_1), .b(8'h1), .out(adder_2_out));  // open: cin, cout
  Subtractor subtractor_1 (.a(in_1), .b(in_2), .out(subtractor_1_out));  // open: bin, bout
  Subtractor subtractor_2 (.a(in_1), .b(8'h1), .out(subtractor_2_out));  // open: bin, bout
  assign and_1_out = in_1 & in_2;  // AND_Gate and_1, 8 bits wide
  assign or_1_out = in_1 | in_2;  // OR_Gate or_1, 8 bits wide
  assign xor_1_out = in_1 ^ in_2;  // XOR_Gate xor_1, 8 bits wide
  Multiplexer #(.select(3), .width(8)) multiplexer_1 (
    .in0(adder_1_out), .in1(adder_2_out), .in2(subtractor_1_out), .in3(subtractor_2_out), .in4(and_1_out),
    .in5(or_1_out), .in6(not_1_out), .in7(xor_1_out), .out(out_4), .sel(in_3));  // open: en
endmodule
